// Logisim project 8cpudeg.circ as structural Verilog: 47 circuits, main circuit main
module play (
  input  PAU,
  input  POW,
  input  RSE,
  input  ADD,
  input  MEN,
  output [7:0] out_6,
  output [7:0] out_7,
  output [7:0] out_8,
  output [7:0] out_9,
  output [7:0] out_10,
  output [7:0] out_11,
  output [7:0] out_12,
  output [7:0] out_13,
  output [15:0] out_14,
  output [7:0] out_15
);

  wire autoadder_1_clock, autoadder_1_resto, not_1_out, rams_1_w, transistor_1_out;

  Transistor transistor_1 (.in(PAU), .out(transistor_1_out), .gate(1'b0));
  AUTOADDER autoadder_1 (
    .RESTO(autoadder_1_resto), .clock(autoadder_1_clock), .POW(POW), .MAN(MEN), .REST(RSE),
    .PAU(transistor_1_out), .ADD(ADD));
  Transistor transistor_2 (.in(out_14[15]), .out(transistor_1_out), .gate(1'b0));
  RAMS rams_1 (
    .W(rams_1_w), .DATAout(out_6), .S(out_8), .CLOCK(autoadder_1_clock), .DATA(out_9), .WE(out_14[8]),
    .CS(out_14[9]));
  not not_1 (not_1_out, autoadder_1_clock);
  Counterp counterp_1 (
    .S(out_15), .CLOCK(not_1_out), .EN(1'b1), .CLEAR(autoadder_1_resto), .CS(1'b1), .EN1(1'b1));  // open: OUTDATA, DATA, PRE
  ROMS roms_1 (.out_2(out_14), .in_1(out_15));
  RAMG ramg_1 (.DATAOUT(out_9), .ADDRESS(out_7), .DATAIN(out_6), .in_3(rams_1_w));
  Counterp counterp_2 (
    .S(out_7), .OUTDATA(out_6), .DATA(out_6), .CLOCK(autoadder_1_clock), .EN(out_14[11]),
    .CLEAR(autoadder_1_resto), .CS(out_14[12]), .EN1(out_14[10]));  // open: PRE
  REGBP regbp_1 (
    .DATAout(out_6), .S(out_10), .CLOCK(autoadder_1_clock), .DATA(out_6), .CLEAR(autoadder_1_resto),
    .WE(out_14[4]), .CS(out_14[5]));  // open: PRE
  ALUP alup_1 (
    .S(out_13), .Sum(out_6), .CP(autoadder_1_clock), .Sel(out_14[6]), .Ina(out_12), .Inb(out_11),
    .EN(out_14[7]));  // open: Carry
  REGBP regbp_2 (
    .DATAout(out_6), .S(out_11), .CLOCK(autoadder_1_clock), .DATA(out_6), .CLEAR(autoadder_1_resto),
    .WE(out_14[2]), .CS(out_14[3]));  // open: PRE
  REGBP regbp_3 (
    .DATAout(out_6), .S(out_12), .CLOCK(autoadder_1_clock), .DATA(out_6), .CLEAR(autoadder_1_resto),
    .WE(out_14[0]), .CS(out_14[1]));  // open: PRE
endmodule

module main (
  input  PAU,
  input  POW,
  input  RSE,
  input  ADD,
  input  MEN,
  output [7:0] out_6,
  output [7:0] out_7,
  output [7:0] out_8,
  output [7:0] out_9,
  output [7:0] out_10,
  output [7:0] out_11,
  output [7:0] out_12,
  output [7:0] out_13,
  output [7:0] out_14,
  output [7:0] out_15,
  output [7:0] out_16,
  output [7:0] out_17,
  output [7:0] out_18,
  output [7:0] out_19,
  output [7:0] out_20,
  output [7:0] out_21,
  output [1:0] out_22,
  output [3:0] out_23,
  output [7:0] out_24,
  output [7:0] out_25,
  output [7:0] out_26,
  output [7:0] out_27,
  output [7:0] out_28,
  output [7:0] out_29,
  output [7:0] out_30,
  output [7:0] out_31,
  output [7:0] out_32,
  output [7:0] out_33,
  output [7:0] out_34
);

  wire AUTO_clock, AUTO_resto, CPUC_hlt, MCC_w, transistor_1_out, transistor_2_out;
  wire [1:0] CPUC_a, CPUC_b, CPUC_bp, CPUC_c, CPUC_cs, CPUC_d, CPUC_di, CPUC_ds, CPUC_dst, CPUC_es, CPUC_ir,
       CPUC_mar, CPUC_mc, CPUC_mdr, CPUC_msr, CPUC_si, CPUC_sp, CPUC_ss, CPUC_t1, CPUC_t2, CPUC_vec;
  wire [2:0] CPUC_op, CPUC_pc;
  wire [3:0] ALU_out_8, undriven;
  wire [7:0] RAM_dataout;
  wire [15:0] CPUC_aa;
  wire [31:0] rom_1_data;

  Transistor transistor_1 (.in(PAU), .out(transistor_1_out), .gate(1'b0));
  AUTOADDER AUTO (
    .RESTO(AUTO_resto), .clock(AUTO_clock), .POW(POW), .MAN(transistor_2_out), .REST(RSE),
    .PAU(transistor_1_out), .ADD(ADD));
  Transistor transistor_2 (.in(MEN), .out(transistor_2_out), .gate(1'b0));
  LED led_1 (.in(transistor_2_out));
  Transistor transistor_3 (.in(CPUC_hlt), .out(transistor_2_out), .gate(1'b0));
  LED led_2 (.in(AUTO_resto));
  LED led_3 (.in(AUTO_clock));
  MC MCC (.W(MCC_w), .DATAout(out_6), .S(out_7), .CLOCK(AUTO_clock), .DATA(RAM_dataout), .IO(CPUC_mc));
  REGBPP IR (
    .DATAout(out_6), .S(out_17), .CLOCK(AUTO_clock), .DATA(out_6), .CLEAR(AUTO_resto), .IO(CPUC_ir));  // open: PRE
  REGBPP DST (
    .DATAout(out_6), .S(out_20), .CLOCK(AUTO_clock), .DATA(out_6), .CLEAR(AUTO_resto), .IO(CPUC_dst));  // open: PRE
  REGBPP SRC (
    .DATAout(out_6), .S(out_24), .CLOCK(AUTO_clock), .DATA(out_6), .CLEAR(AUTO_resto), .IO(out_22));  // open: PRE
  REGBPP CS (
    .DATAout(out_6), .S(out_25), .CLOCK(AUTO_clock), .DATA(out_6), .CLEAR(AUTO_resto), .IO(CPUC_cs));  // open: PRE
  ROM #(.addrWidth(16), .dataWidth(32)) rom_1 (.addr(CPUC_aa), .data(rom_1_data));
  RAMP RAM (.DATAOUT(RAM_dataout), .ADDRESS({out_8, out_9}), .DATAIN(out_6), .in_3(MCC_w));
  REGBPP DS (
    .DATAout(out_6), .S(out_26), .CLOCK(AUTO_clock), .DATA(out_6), .CLEAR(AUTO_resto), .IO(CPUC_ds));  // open: PRE
  REGBPP MSR (
    .DATAout(out_6), .S(out_8), .CLOCK(AUTO_clock), .DATA(out_6), .CLEAR(AUTO_resto), .IO(CPUC_msr));  // open: PRE
  REGBPP SS (
    .DATAout(out_6), .S(out_27), .CLOCK(AUTO_clock), .DATA(out_6), .CLEAR(AUTO_resto), .IO(CPUC_ss));  // open: PRE
  REGBPP MAR (
    .DATAout(out_6), .S(out_9), .CLOCK(AUTO_clock), .DATA(out_6), .CLEAR(AUTO_resto), .IO(CPUC_mar));  // open: PRE
  REGBPP ES (.DATAout(out_6), .S(out_28), .CLOCK(AUTO_clock), .DATA(out_6), .CLEAR(AUTO_resto));  // open: PRE, IO
  REGBPP MDR (
    .DATAout(out_6), .S(out_10), .CLOCK(AUTO_clock), .DATA(out_6), .CLEAR(AUTO_resto), .IO(CPUC_mdr));  // open: PRE
  CONTROL CPUC (
    .A(CPUC_a), .VEC(CPUC_vec), .B(CPUC_b), .T1(CPUC_t1), .C(CPUC_c), .T2(CPUC_t2), .D(CPUC_d), .CYC(out_23),
    .AA(CPUC_aa), .HLT(CPUC_hlt), .OP(CPUC_op), .PC(CPUC_pc), .SRC(out_22), .DST(CPUC_dst), .IR(CPUC_ir),
    .CS(CPUC_cs), .DS(CPUC_ds), .SS(CPUC_ss), .ES(CPUC_es), .MSR(CPUC_msr), .MAR(CPUC_mar), .MDR(CPUC_mdr),
    .MC(CPUC_mc), .BP(CPUC_bp), .SP(CPUC_sp), .SI(CPUC_si), .DI(CPUC_di), .PSW(ALU_out_8), .R1(out_17),
    .CLOCK(AUTO_clock), .CLEAR(AUTO_resto), .DD(rom_1_data), .ALU(undriven), .R2(out_20), .R3(out_24));
  REGBPP DI (
    .DATAout(out_6), .S(out_29), .CLOCK(AUTO_clock), .DATA(out_6), .CLEAR(AUTO_resto), .IO(CPUC_di));  // open: PRE
  PCP PC (
    .OUTDATA(out_6), .S(out_11), .EN(CPUC_pc), .DATA(out_6), .CLEAR(AUTO_resto), .CLOCK(AUTO_clock));  // open: PRE
  REGBPP SI (
    .DATAout(out_6), .S(out_30), .CLOCK(AUTO_clock), .DATA(out_6), .CLEAR(AUTO_resto), .IO(CPUC_si));  // open: PRE
  ALUPPP ALU (
    .out_8(ALU_out_8), .S(out_12), .Sum(out_6), .CLOCK(AUTO_clock), .Sel(CPUC_op), .Ina(out_14),
    .Inb(out_13), .EN(undriven), .CLEAR(AUTO_resto));  // open: PRE
  REGBPP SP (
    .DATAout(out_6), .S(out_31), .CLOCK(AUTO_clock), .DATA(out_6), .CLEAR(AUTO_resto), .IO(CPUC_sp));  // open: PRE
  REGBPP BREG (
    .DATAout(out_6), .S(out_13), .CLOCK(AUTO_clock), .DATA(out_6), .CLEAR(AUTO_resto), .IO(CPUC_b));  // open: PRE
  REGBPP BP (.DATAout(out_6), .S(out_32), .CLOCK(AUTO_clock), .DATA(out_6), .CLEAR(AUTO_resto));  // open: PRE, IO
  REGBPP AREG (
    .DATAout(out_6), .S(out_14), .CLOCK(AUTO_clock), .DATA(out_6), .CLEAR(AUTO_resto), .IO(CPUC_a));  // open: PRE
  REGBPP VEC (
    .DATAout(out_6), .S(out_33), .CLOCK(AUTO_clock), .DATA(out_6), .CLEAR(AUTO_resto), .IO(CPUC_vec));  // open: PRE
  REGBPP CREG (
    .DATAout(out_6), .S(out_15), .CLOCK(AUTO_clock), .DATA(out_6), .CLEAR(AUTO_resto), .IO(CPUC_c));  // open: PRE
  REGBPP DREG (
    .DATAout(out_6), .S(out_16), .CLOCK(AUTO_clock), .DATA(out_6), .CLEAR(AUTO_resto), .IO(CPUC_d));  // open: PRE
  REGBPP T1 (
    .DATAout(out_6), .S(out_18), .CLOCK(AUTO_clock), .DATA(out_6), .CLEAR(AUTO_resto), .IO(CPUC_t1));  // open: PRE
  REGBPP T2 (.DATAout(out_6), .S(out_21), .CLOCK(AUTO_clock), .CLEAR(AUTO_resto), .IO(CPUC_t2));  // open: PRE, DATA
  REGBPP ERA (.DATAout(out_6), .S(out_34), .CLOCK(AUTO_clock), .DATA(out_6), .CLEAR(AUTO_resto));  // open: PRE, IO

  assign out_19 = out_16;

  // Notes on the sheet:
  //   contents of rom_1 (hex, n*v repeats v):
  //   8040 1c0a4 8040 1c0c4 8040 1c0e4 10*40000000 8040 1c0a4 8040 1c0c4 8040 1c0e4 10*40000000 8040 1c0a4
  //   8040 1c0c4 8040 1c0e4 10*40000000 8040 1c0a4 8040 1c0c4 8040 1c0e4 10*40000000 8040 1c0a4 8040 1c0c4
  //   8040 1c0e4 10*40000000 8040 1c0a4 8040 1c0c4 8040 1c0e4 10*40000000 8040 1c0a4 8040 1c0c4 8040 1c0e4
  //   10*40000000 8040 1c0a4 8040 1c0c4 8040 1c0e4 10*40000000 8040 1c0a4 8040 1c0c4 8040 1c0e4
  //   10*40000000 8040 1c0a4 8040 1c0c4 8040 1c0e4 10*40000000 8040 1c0a4 8040 1c0c4 8040 1c0e4
  //   10*40000000 8040 1c0a4 8040 1c0c4 8040 1c0e4 10*40000000 8040 1c0a4 8040 1c0c4 8040 1c0e4
  //   10*40000000 8040 1c0a4 8040 1c0c4 8040 1c0e4 10*40000000 8040 1c0a4 8040 1c0c4 8040 1c0e4
  //   10*40000000 8040 1c0a4 8040 1c0c4 8040 1c0e4 10*40000000 8040 1c0a4 8040 1c0c4 8040 1c0e4
  //   10*40000000 8040 1c0a4 8040 1c0c4 8040 1c0e4 10*40000000 8040 1c0a4 8040 1c0c4 8040 1c0e4
  //   10*40000000 8040 1c0a4 8040 1c0c4 8040 1c0e4 10*40000000 8040 1c0a4 8040 1c0c4 8040 1c0e4
  //   10*40000000 8040 1c0a4 8040 1c0c4 8040 1c0e4 10*40000000 8040 1c0a4 8040 1c0c4 8040 1c0e4
  //   10*40000000 8040 1c0a4 8040 1c0c4 8040 1c0e4 10*40000000 8040 1c0a4 8040 1c0c4 8040 1c0e4
  //   10*40000000 8040 1c0a4 8040 1c0c4 8040 1c0e4 10*40000000 8040 1c0a4 8040 1c0c4 8040 1c0e4
  //   10*40000000 8040 1c0a4 8040 1c0c4 8040 1c0e4 10*40000000 8040 1c0a4 8040 1c0c4 8040 1c0e4
  //   10*40000000 8040 1c0a4 8040 1c0c4 8040 1c0e4 10*40000000 8040 1c0a4 8040 1c0c4 8040 1c0e4
  //   10*40000000 8040 1c0a4 8040 1c0c4 8040 1c0e4 10*40000000 8040 1c0a4 8040 1c0c4 8040 1c0e4
  //   10*40000000 8040 1c0a4 8040 1c0c4 8040 1c0e4 10*40000000 8040 1c0a4 8040 1c0c4 8040 1c0e4
  //   10*40000000 8040 1c0a4 8040 1c0c4 8040 1c0e4 10*40000000 8040 1c0a4 8040 1c0c4 8040 1c0e4
  //   10*40000000 8040 1c0a4 8040 1c0c4 8040 1c0e4 10*40000000 8040 1c0a4 8040 1c0c4 8040 1c0e4
  //   10*40000000 8040 1c0a4 8040 1c0c4 8040 1c0e4 10*40000000 8040 1c0a4 8040 1c0c4 8040 1c0e4
  //   10*40000000 8040 1c0a4 8040 1c0c4 8040 1c0e4 10*40000000 8040 1c0a4 8040 1c0c4 8040 1c0e4
  //   10*40000000 8040 1c0a4 8040 1c0c4 8040 1c0e4 10*40000000 8040 1c0a4 8040 1c0c4 8040 1c0e4
  //   10*40000000 8040 1c0a4 8040 1c0c4 8040 1c0e4 10*40000000 8040 1c0a4 8040 1c0c4 8040 1c0e4
  //   10*40000000 8040 1c0a4 8040 1c0c4 8040 1c0e4 10*40000000 8040 1c0a4 8040 1c0c4 8040 1c0e4
  //   10*40000000 8040 1c0a4 8040 1c0c4 8040 1c0e4 10*40000000 8040 1c0a4 8040 1c0c4 8040 1c0e4
  //   10*40000000 8040 1c0a4 8040 1c0c4 8040 1c0e4 10*40000000 8040 1c0a4 8040 1c0c4 8040 1c0e4
  //   10*40000000 8040 1c0a4 8040 1c0c4 8040 1c0e4 10*40000000 8040 1c0a4 8040 1c0c4 8040 1c0e4
  //   10*40000000 8040 1c0a4 8040 1c0c4 8040 1c0e4 10*40000000 8040 1c0a4 8040 1c0c4 8040 1c0e4
  //   10*40000000 8040 1c0a4 8040 1c0c4 8040 1c0e4 10*40000000 8040 1c0a4 8040 1c0c4 8040 1c0e4
  //   10*40000000 8040 1c0a4 8040 1c0c4 8040 1c0e4 10*40000000 8040 1c0a4 8040 1c0c4 8040 1c0e4
  //   10*40000000 8040 1c0a4 8040 1c0c4 8040 1c0e4 10*40000000 8040 1c0a4 8040 1c0c4 8040 1c0e4
  //   10*40000000 8040 1c0a4 8040 1c0c4 8040 1c0e4 10*40000000 8040 1c0a4 8040 1c0c4 8040 1c0e4
  //   10*40000000 8040 1c0a4 8040 1c0c4 8040 1c0e4 10*40000000 8040 1c0a4 8040 1c0c4 8040 1c0e4
  //   10*40000000 8040 1c0a4 8040 1c0c4 8040 1c0e4 10*40000000 8040 1c0a4 8040 1c0c4 8040 1c0e4
  //   10*40000000 8040 1c0a4 8040 1c0c4 8040 1c0e4 10*40000000 8040 1c0a4 8040 1c0c4 8040 1c0e4
  //   10*40000000 8040 1c0a4 8040 1c0c4 8040 1c0e4 10*40000000 8040 1c0a4 8040 1c0c4 8040 1c0e4
  //   10*40000000 8040 1c0a4 8040 1c0c4 8040 1c0e4 10*40000000 8040 1c0a4 8040 1c0c4 8040 1c0e4
  //   10*40000000 8040 1c0a4 8040 1c0c4 8040 1c0e4 10*40000000 8040 1c0a4 8040 1c0c4 8040 1c0e4
  //   10*40000000 8040 1c0a4 8040 1c0c4 8040 1c0e4 10*40000000 8040 1c0a4 8040 1c0c4 8040 1c0e4
  //   10*40000000 8040 1c0a4 8040 1c0c4 8040 1c0e4 10*40000000 8040 1c0a4 8040 1c0c4 8040 1c0e4
  //   10*40000000 8040 1c0a4 8040 1c0c4 8040 1c0e4 10*40000000 8040 1c0a4 8040 1c0c4 8040 1c0e4
  //   10*40000000 8040 1c0a4 8040 1c0c4 8040 1c0e4 10*40000000 8040 1c0a4 8040 1c0c4 8040 1c0e4
  //   10*40000000 8040 1c0a4 8040 1c0c4 8040 1c0e4 10*40000000 8040 1c0a4 8040 1c0c4 8040 1c0e4
  //   10*40000000 8040 1c0a4 8040 1c0c4 8040 1c0e4 10*40000000 8040 1c0a4 8040 1c0c4 8040 1c0e4 10*4000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
endmodule

module Halfadder (
  input  Ina,
  input  Inb,
  output Sum,
  output Carry
);

  and and_1 (Carry, Ina, Inb);
  xor xor_1 (Sum, Ina, Inb);
endmodule

module Fulladder (
  input  CarryIn,
  input  Ina,
  input  Inb,
  output Sum,
  output Carryout
);

  wire halfadder_1_carry, halfadder_1_sum, halfadder_2_carry;

  Halfadder halfadder_1 (.Sum(halfadder_1_sum), .Carry(halfadder_1_carry), .Ina(Ina), .Inb(Inb));
  Halfadder halfadder_2 (.Sum(Sum), .Carry(halfadder_2_carry), .Ina(CarryIn), .Inb(halfadder_1_sum));
  or or_1 (Carryout, halfadder_2_carry, halfadder_1_carry);
endmodule

module Inv (
  input  Sel,
  input  Ina,
  output Outa
);

  xor xor_1 (Outa, Sel, Ina);
endmodule

module Inv8 (
  input  Sel,
  input  [7:0] Ina,
  output [7:0] Outa
);

  Inv inv_1 (.Outa(Outa[0]), .Sel(Sel), .Ina(Ina[0]));
  Inv inv_2 (.Outa(Outa[1]), .Sel(Sel), .Ina(Ina[1]));
  Inv inv_3 (.Outa(Outa[2]), .Sel(Sel), .Ina(Ina[2]));
  Inv inv_4 (.Outa(Outa[3]), .Sel(Sel), .Ina(Ina[3]));
  Inv inv_5 (.Outa(Outa[4]), .Sel(Sel), .Ina(Ina[4]));
  Inv inv_6 (.Outa(Outa[5]), .Sel(Sel), .Ina(Ina[5]));
  Inv inv_7 (.Outa(Outa[6]), .Sel(Sel), .Ina(Ina[6]));
  Inv inv_8 (.Outa(Outa[7]), .Sel(Sel), .Ina(Ina[7]));
endmodule

module Add8 (
  input  CarryIn,
  input  [7:0] Ina,
  input  [7:0] Inb,
  output [7:0] out_4,
  output Carryout
);

  wire fulladder_1_carryout, fulladder_2_carryout, fulladder_3_carryout, fulladder_4_carryout,
       fulladder_5_carryout, fulladder_6_carryout, fulladder_7_carryout;

  Fulladder fulladder_1 (
    .Sum(out_4[0]), .Carryout(fulladder_1_carryout), .CarryIn(CarryIn), .Ina(Ina[0]), .Inb(Inb[0]));
  Fulladder fulladder_2 (
    .Sum(out_4[1]), .Carryout(fulladder_2_carryout), .CarryIn(fulladder_1_carryout), .Ina(Ina[1]),
    .Inb(Inb[1]));
  Fulladder fulladder_3 (
    .Sum(out_4[2]), .Carryout(fulladder_3_carryout), .CarryIn(fulladder_2_carryout), .Ina(Ina[2]),
    .Inb(Inb[2]));
  Fulladder fulladder_4 (
    .Sum(out_4[3]), .Carryout(fulladder_4_carryout), .CarryIn(fulladder_3_carryout), .Ina(Ina[3]),
    .Inb(Inb[3]));
  Fulladder fulladder_5 (
    .Sum(out_4[4]), .Carryout(fulladder_5_carryout), .CarryIn(fulladder_4_carryout), .Ina(Ina[4]),
    .Inb(Inb[4]));
  Fulladder fulladder_6 (
    .Sum(out_4[5]), .Carryout(fulladder_6_carryout), .CarryIn(fulladder_5_carryout), .Ina(Ina[5]),
    .Inb(Inb[5]));
  Fulladder fulladder_7 (
    .Sum(out_4[6]), .Carryout(fulladder_7_carryout), .CarryIn(fulladder_6_carryout), .Ina(Ina[6]),
    .Inb(Inb[6]));
  Fulladder fulladder_8 (
    .Sum(out_4[7]), .Carryout(Carryout), .CarryIn(fulladder_7_carryout), .Ina(Ina[7]), .Inb(Inb[7]));
endmodule

module Add8p (
  input  Sel,
  input  [7:0] Ina,
  input  [7:0] Inb,
  output [7:0] Sum,
  output Carry
);

  wire add8_1_carryout, not_1_out;
  wire [7:0] inv8_1_outa;

  Inv8 inv8_1 (.Outa(inv8_1_outa), .Sel(Sel), .Ina(Inb));
  Add8 add8_1 (.out_4(Sum), .Carryout(add8_1_carryout), .CarryIn(Sel), .Ina(Ina), .Inb(inv8_1_outa));
  not not_1 (not_1_out, Sel);
  and and_1 (Carry, not_1_out, add8_1_carryout);
endmodule

module Digital (
  input  [3:0] in_1
);

  wire [7:0] rom_1_data;

  ROM #(.addrWidth(4)) rom_1 (.addr(in_1), .data(rom_1_data));
  _7_Segment_Display u_7_segment_display_1 (
    .g(rom_1_data[0]), .f(rom_1_data[1]), .a(rom_1_data[2]), .b(rom_1_data[3]), .e(rom_1_data[4]),
    .d(rom_1_data[5]), .c(rom_1_data[6]), .dp(rom_1_data[7]));

  // Notes on the sheet:
  //   contents of rom_1 (hex, n*v repeats v):
  //   7e 48 3d 6d 4b 67 77 4c 7f 6f
endmodule

module RSFF (
  input  Clear,
  input  Reet,
  input  Set,
  input  Pre,
  output Q,
  output AQ
);

  nor nor_1 (Q, Reet, Clear, AQ);
  nor nor_2 (AQ, Q, Pre, Set);
endmodule

module DFF (
  input  Clear,
  input  DATA,
  input  EN,
  input  Pre,
  output Q,
  output AQ
);

  wire and_1_out, and_2_out, not_1_out;

  not not_1 (not_1_out, DATA);
  and and_1 (and_1_out, not_1_out, EN);
  and and_2 (and_2_out, EN, DATA);
  RSFF rsff_1 (.Q(Q), .AQ(AQ), .Reet(and_1_out), .Set(and_2_out), .Clear(Clear), .Pre(Pre));
endmodule

module DFFP (
  input  Clear,
  input  Data,
  input  En,
  input  Pre,
  output OUTP,
  output OUTAP
);

  wire dff_1_q, not_1_out;

  not not_1 (not_1_out, En);
  DFF dff_1 (.Q(dff_1_q), .Clear(Clear), .Pre(Pre), .DATA(Data), .EN(not_1_out));  // open: AQ
  DFF dff_2 (.Q(OUTP), .AQ(OUTAP), .Clear(Clear), .Pre(Pre), .DATA(dff_1_q), .EN(En));
endmodule

module TFF (
  input  Clear,
  input  Ina,
  input  Pre,
  output Outa,
  output Outb
);

  DFFP dffp_1 (.OUTP(Outa), .OUTAP(Outb), .Data(Outb), .En(Ina), .Clear(Clear), .Pre(Pre));
endmodule

module Count (
  input  Clear,
  input  EN,
  input  CLOCK,
  input  Pre,
  output [7:0] Outs
);

  wire and_1_out, tff_1_outb, tff_2_outb, tff_3_outb, tff_4_outb, tff_5_outb, tff_6_outb, tff_7_outb;

  and and_1 (and_1_out, EN, CLOCK);
  TFF tff_1 (.Outa(Outs[0]), .Outb(tff_1_outb), .Ina(and_1_out), .Clear(Clear), .Pre(Pre));
  TFF tff_2 (.Outa(Outs[1]), .Outb(tff_2_outb), .Ina(tff_1_outb), .Clear(Clear), .Pre(Pre));
  TFF tff_3 (.Outa(Outs[2]), .Outb(tff_3_outb), .Ina(tff_2_outb), .Clear(Clear), .Pre(Pre));
  TFF tff_4 (.Outa(Outs[3]), .Outb(tff_4_outb), .Ina(tff_3_outb), .Clear(Clear), .Pre(Pre));
  TFF tff_5 (.Outa(Outs[4]), .Outb(tff_5_outb), .Ina(tff_4_outb), .Clear(Clear), .Pre(Pre));
  TFF tff_6 (.Outa(Outs[5]), .Outb(tff_6_outb), .Ina(tff_5_outb), .Clear(Clear), .Pre(Pre));
  TFF tff_7 (.Outa(Outs[6]), .Outb(tff_7_outb), .Ina(tff_6_outb), .Clear(Clear), .Pre(Pre));
  TFF tff_8 (.Outa(Outs[7]), .Ina(tff_7_outb), .Clear(Clear), .Pre(Pre));  // open: Outb
endmodule

module REGB (
  input  [7:0] DATA,
  input  Clear,
  input  Pre,
  input  CLOCK,
  output [7:0] DATAOUT
);

  DFFP dffp_1 (.OUTP(DATAOUT[0]), .Data(DATA[0]), .En(CLOCK), .Clear(Clear), .Pre(Pre));  // open: OUTAP
  DFFP dffp_2 (.OUTP(DATAOUT[1]), .Data(DATA[1]), .En(CLOCK), .Clear(Clear), .Pre(Pre));  // open: OUTAP
  DFFP dffp_3 (.OUTP(DATAOUT[2]), .Data(DATA[2]), .En(CLOCK), .Clear(Clear), .Pre(Pre));  // open: OUTAP
  DFFP dffp_4 (.OUTP(DATAOUT[3]), .Data(DATA[3]), .En(CLOCK), .Clear(Clear), .Pre(Pre));  // open: OUTAP
  DFFP dffp_5 (.OUTP(DATAOUT[4]), .Data(DATA[4]), .En(CLOCK), .Clear(Clear), .Pre(Pre));  // open: OUTAP
  DFFP dffp_6 (.OUTP(DATAOUT[5]), .Data(DATA[5]), .En(CLOCK), .Clear(Clear), .Pre(Pre));  // open: OUTAP
  DFFP dffp_7 (.OUTP(DATAOUT[6]), .Data(DATA[6]), .En(CLOCK), .Clear(Clear), .Pre(Pre));  // open: OUTAP
  DFFP dffp_8 (.OUTP(DATAOUT[7]), .Data(DATA[7]), .En(CLOCK), .Clear(Clear), .Pre(Pre));  // open: OUTAP
endmodule

module GATA8 (
  input  [7:0] DATA,
  input  SEL,
  output [7:0] DATAOUT
);

  assign DATAOUT[0] = SEL ? DATA[0] : 1'bz;  // Controlled_Buffer controlled_buffer_1
  assign DATAOUT[1] = SEL ? DATA[1] : 1'bz;  // Controlled_Buffer controlled_buffer_2
  assign DATAOUT[2] = SEL ? DATA[2] : 1'bz;  // Controlled_Buffer controlled_buffer_3
  assign DATAOUT[3] = SEL ? DATA[3] : 1'bz;  // Controlled_Buffer controlled_buffer_4
  assign DATAOUT[4] = SEL ? DATA[4] : 1'bz;  // Controlled_Buffer controlled_buffer_5
  assign DATAOUT[5] = SEL ? DATA[5] : 1'bz;  // Controlled_Buffer controlled_buffer_6
  assign DATAOUT[6] = SEL ? DATA[6] : 1'bz;  // Controlled_Buffer controlled_buffer_7
  assign DATAOUT[7] = SEL ? DATA[7] : 1'bz;  // Controlled_Buffer controlled_buffer_8
endmodule

module REGBP (
  input  [7:0] DATA,
  input  CLOCK,
  input  PRE,
  input  CLEAR,
  input  WE,
  input  CS,
  output [7:0] S,
  output [7:0] DATAout
);

  wire and_1_out, and_2_out, not_1_out;

  and and_1 (and_1_out, WE, CS, CLOCK);
  REGB regb_1 (.DATAOUT(S), .DATA(DATA), .Pre(PRE), .CLOCK(and_1_out), .Clear(CLEAR));
  and and_2 (and_2_out, not_1_out, CS);
  GATA8 gata8_1 (.DATAOUT(DATAout), .DATA(S), .SEL(and_2_out));
  not not_1 (not_1_out, WE);
endmodule

module REG8 (
  input  CLEAR,
  input  EN,
  input  CLOCK,
  input  [7:0] DATA,
  input  PRE,
  input  CS,
  input  [2:0] ADDRE,
  output [7:0] DATAout
);

  wire [7:0] equal38_1_outo;

  EQUAL38 equal38_1 (.OUTO(equal38_1_outo), .C(ADDRE[2]), .B(ADDRE[1]), .A(ADDRE[0]), .EN(CS));
  REGBP regbp_1 (
    .DATAout(DATAout), .PRE(PRE), .CLOCK(CLOCK), .DATA(DATA), .CLEAR(CLEAR), .WE(EN), .CS(equal38_1_outo[7]));  // open: S
  REGBP regbp_2 (
    .DATAout(DATAout), .PRE(PRE), .CLOCK(CLOCK), .DATA(DATA), .CLEAR(CLEAR), .WE(EN), .CS(equal38_1_outo[6]));  // open: S
  REGBP regbp_3 (
    .DATAout(DATAout), .PRE(PRE), .CLOCK(CLOCK), .DATA(DATA), .CLEAR(CLEAR), .WE(EN), .CS(equal38_1_outo[5]));  // open: S
  REGBP regbp_4 (
    .DATAout(DATAout), .PRE(PRE), .CLOCK(CLOCK), .DATA(DATA), .CLEAR(CLEAR), .WE(EN), .CS(equal38_1_outo[4]));  // open: S
  REGBP regbp_5 (
    .DATAout(DATAout), .PRE(PRE), .CLOCK(CLOCK), .DATA(DATA), .CLEAR(CLEAR), .WE(EN), .CS(equal38_1_outo[3]));  // open: S
  REGBP regbp_6 (
    .DATAout(DATAout), .PRE(PRE), .CLOCK(CLOCK), .DATA(DATA), .CLEAR(CLEAR), .WE(EN), .CS(equal38_1_outo[2]));  // open: S
  REGBP regbp_7 (
    .DATAout(DATAout), .PRE(PRE), .CLOCK(CLOCK), .DATA(DATA), .CLEAR(CLEAR), .WE(EN), .CS(equal38_1_outo[1]));  // open: S
  REGBP regbp_8 (
    .DATAout(DATAout), .PRE(PRE), .CLOCK(CLOCK), .DATA(DATA), .CLEAR(CLEAR), .WE(EN), .CS(equal38_1_outo[0]));  // open: S
endmodule

module EQUAL38 (
  input  C,
  input  B,
  input  A,
  input  EN,
  output [7:0] OUTO
);

  wire not_1_out, not_2_out, not_3_out;

  not not_1 (not_1_out, C);
  not not_2 (not_2_out, B);
  not not_3 (not_3_out, A);
  and and_1 (OUTO[7], EN, C, B, A);
  and and_2 (OUTO[6], EN, C, B, not_3_out);
  and and_3 (OUTO[5], EN, C, not_2_out, A);
  and and_4 (OUTO[4], EN, C, not_2_out, not_3_out);
  and and_5 (OUTO[3], EN, not_1_out, B, A);
  and and_6 (OUTO[2], EN, not_1_out, B, not_3_out);
  and and_7 (OUTO[1], EN, not_1_out, not_2_out, A);
  and and_8 (OUTO[0], EN, not_1_out, not_2_out, not_3_out);
endmodule

module RGB8to16 (
  input  [15:0] DATA,
  input  Pre,
  input  Clear,
  input  CLOCK,
  input  [2:0] ADDREE,
  input  EN,
  input  CS,
  output [15:0] DATAOUT
);

  REG8 reg8_1 (
    .DATAout(DATAOUT[15:8]), .ADDRE(ADDREE), .CS(CS), .DATA(DATA[15:8]), .CLEAR(Clear), .EN(EN),
    .CLOCK(CLOCK), .PRE(Pre));
  REG8 reg8_2 (
    .DATAout(DATAOUT[7:0]), .ADDRE(ADDREE), .CS(CS), .DATA(DATA[7:0]), .CLEAR(Clear), .EN(EN), .CLOCK(CLOCK),
    .PRE(Pre));
endmodule

module RGB16 (
  input  Clear,
  input  Pre,
  input  CLOCK,
  input  [7:0] DATA,
  input  CS,
  input  [3:0] ADDRESS,
  input  EN,
  output [7:0] DATAOUT
);

  wire [1:0] equal12_1_out_3;

  EQUAL12 equal12_1 (.out_3(equal12_1_out_3), .INA(ADDRESS[0]), .EN(CS));
  REG8 reg8_1 (
    .DATAout(DATAOUT), .ADDRE(ADDRESS[3:1]), .CS(equal12_1_out_3[1]), .DATA(DATA), .CLEAR(Clear), .EN(EN),
    .CLOCK(CLOCK), .PRE(Pre));
  REG8 reg8_2 (
    .DATAout(DATAOUT), .ADDRE(ADDRESS[3:1]), .CS(equal12_1_out_3[0]), .DATA(DATA), .CLEAR(Clear), .EN(EN),
    .CLOCK(CLOCK), .PRE(Pre));
endmodule

module EQUAL12 (
  input  INA,
  input  EN,
  output [1:0] out_3
);

  wire not_1_out;

  not not_1 (not_1_out, INA);
  and and_1 (out_3[1], EN, INA);
  and and_2 (out_3[0], EN, not_1_out);
endmodule

module ALU (
  input  Sel,
  input  [7:0] Ina,
  input  [7:0] Inb,
  output [7:0] Sum,
  output Carry
);

  wire add8_1_carryout, not_1_out;
  wire [7:0] inv8_1_outa;

  Inv8 inv8_1 (.Outa(inv8_1_outa), .Sel(Sel), .Ina(Inb));
  Add8 add8_1 (.out_4(Sum), .Carryout(add8_1_carryout), .CarryIn(Sel), .Ina(Ina), .Inb(inv8_1_outa));
  not not_1 (not_1_out, Sel);
  and and_1 (Carry, not_1_out, add8_1_carryout);
endmodule

module SWITH (
  input  REST,
  input  POW,
  input  MAN,
  input  PUL,
  input  HLT,
  output OUTOUT,
  output RES
);

  wire and_1_out, and_2_out, and_3_out, clock_1_out, not_1_out, not_2_out, not_3_out, not_5_out;

  Clock clock_1 (.out(clock_1_out));
  not not_1 (not_1_out, REST);
  not not_2 (not_2_out, POW);
  not not_3 (not_3_out, MAN);
  // NOT_Gate not_4 has open pins: in=PUL, out=open
  not not_5 (not_5_out, HLT);
  and and_1 (and_1_out, POW, not_1_out, not_3_out, not_5_out, clock_1_out);
  and and_2 (and_2_out, POW, not_1_out, MAN, not_5_out, PUL);
  or or_1 (OUTOUT, and_1_out, and_2_out);
  and and_3 (and_3_out, POW, REST);
  or or_2 (RES, and_3_out, not_2_out);
endmodule

module AUTOADDER (
  input  POW,
  input  REST,
  input  PAU,
  input  ADD,
  input  MAN,
  output RESTO,
  output clock
);

  wire not_1_out, switch_1_p2, switch_2_p2, switch_3_p2, switch_4_p2, switch_5_p2, switch_6_p2,
       transistor_1_out, transistor_3_out, transistor_5_out, transistor_7_out, transistor_9_out;
  wire [7:0] alu_1_sum, count_1_outs, regbp_1_dataout, rom1_1_out_2;

  // Switch switch_1: pin names not known; wires that end beside it: 1'b1, switch_1_p2
  // Switch switch_2: pin names not known; wires that end beside it: 1'b1, switch_2_p2
  // Switch switch_3: pin names not known; wires that end beside it: 1'b1, switch_3_p2
  Transistor transistor_1 (.in(switch_1_p2), .out(transistor_1_out), .gate(1'b0));
  Transistor transistor_2 (.in(PAU), .out(transistor_1_out), .gate(1'b0));
  Transistor transistor_3 (.in(switch_2_p2), .out(transistor_3_out), .gate(1'b0));
  Transistor transistor_4 (.in(ADD), .out(transistor_3_out), .gate(1'b0));
  Transistor transistor_5 (.in(switch_3_p2), .out(transistor_5_out), .gate(1'b0));
  Transistor transistor_6 (.in(POW), .out(transistor_5_out), .gate(1'b0));
  Transistor transistor_7 (.in(switch_4_p2), .out(transistor_7_out), .gate(1'b0));
  // Switch switch_4: pin names not known; wires that end beside it: 1'b1, switch_4_p2
  Transistor transistor_8 (.in(MAN), .out(transistor_7_out), .gate(1'b0));
  // Switch switch_5: pin names not known; wires that end beside it: 1'b1, switch_5_p2
  SWITH swith_1 (
    .OUTOUT(clock), .RES(RESTO), .REST(transistor_9_out), .POW(transistor_5_out), .MAN(transistor_7_out),
    .PUL(transistor_3_out), .HLT(transistor_1_out));
  Transistor transistor_9 (.in(switch_5_p2), .out(transistor_9_out), .gate(1'b0));
  Transistor transistor_10 (.in(REST), .out(transistor_9_out), .gate(1'b0));
  ROM1 rom1_1 (.out_2(rom1_1_out_2), .in_1(count_1_outs));
  ALU alu_1 (.Sum(alu_1_sum), .Ina(rom1_1_out_2), .Inb(regbp_1_dataout));  // open: Carry, Sel
  // Switch switch_6: pin names not known; wires that end beside it: 1'b1, switch_6_p2
  not not_1 (not_1_out, clock);
  Count count_1 (.Outs(count_1_outs), .EN(switch_6_p2), .CLOCK(not_1_out), .Clear(RESTO));  // open: Pre
  REGBP regbp_1 (
    .DATAout(regbp_1_dataout), .CLOCK(clock), .DATA(alu_1_sum), .CLEAR(RESTO), .WE(clock), .CS(switch_6_p2));  // open: S, PRE
endmodule

module ROM1 (
  input  [7:0] in_1,
  output [7:0] out_2
);

  ROM rom_1 (.addr(in_1), .data(out_2));

  // Notes on the sheet:
  //   contents of rom_1 (hex, n*v repeats v):
  //   0 1 2 3 4 5 6 7 8 9 10 11 12 13 14 15 16 17 18 19 20 21 22 23 24 25 26 27 28 29 30 31 20 21 22 23 24
  //   25 26 27 28 29 2a 2b 2c 2d 2e 2f 30 31 32 33 34 35 36 37 38 39 3a 3b 3c 3d 3e 3f 40 41 42 43 44 45
  //   46 47 48 49 4a 4b 4c 4d 4e 4f 50 51 52 53 54 55 56 57 58 59 5a 5b 5c 5d 5e 5f 60 61 62 63 64 65 66
  //   67 68 69 6a 6b 6c 6d 6e 6f 70 71 72 73 74 75 76 77 78 79 7a 7b 7c 7d 7e 7f 80 81 82 83 84 85 86 87
  //   88 89 8a 8b 8c 8d 8e 8f 90 91 92 93 94 95 96 97 98 99 9a 9b 9c 9d 9e 9f a0 a1 a2 a3 a4 a5 a6 a7 a8
  //   a9 aa ab ac ad ae af b0 b1 b2 b3 b4 b5 b6 b7 b8 b9 ba bb bc bd be bf c0 c1 c2 c3 c4 c5 c6 c7 c8 c9
  //   ca cb cc cd ce cf d0 d1 d2 d3 d4 d5 d6 d7 d8 d9 da db dc dd de df e0 e1 e2 e3 e4 e5 e6 e7 e8 e9 ea
  //   eb ec ed ee ef f0 f1 f2 f3 f4 f5 f6 f7 f8 f9 fa fb fc fd fe ff
endmodule

module Counterp (
  input  CLEAR,
  input  EN,
  input  EN1,
  input  CLOCK,
  input  [7:0] DATA,
  input  CS,
  input  PRE,
  output [7:0] S,
  output [7:0] OUTDATA
);

  wire not_1_out;
  wire [7:0] alupp_1_s, gata8_1_dataout;

  GATA8 gata8_1 (.DATAOUT(gata8_1_dataout), .DATA(DATA), .SEL(not_1_out));
  REGBP regbp_1 (
    .DATAout(OUTDATA), .S(S), .PRE(PRE), .CLOCK(CLOCK), .DATA(gata8_1_dataout), .CLEAR(CLEAR), .WE(EN),
    .CS(CS));
  not not_1 (not_1_out, EN1);
  ALUPP alupp_1 (.S(alupp_1_s), .Sel(3'b000), .Ina(S), .Inb(8'h1));  // open: out_8, Sum, EN, in_3, in_5, in_6
  GATA8 gata8_2 (.DATAOUT(gata8_1_dataout), .DATA(alupp_1_s), .SEL(EN1));
endmodule

module RAMS (
  input  CLOCK,
  input  [7:0] DATA,
  input  WE,
  input  CS,
  output W,
  output [7:0] S,
  output [7:0] DATAout
);

  wire and_2_out, not_1_out;

  and and_1 (W, WE, CS, CLOCK);
  and and_2 (and_2_out, not_1_out, CS);
  GATA8 gata8_1 (.DATAOUT(DATAout), .DATA(DATA), .SEL(and_2_out));
  not not_1 (not_1_out, WE);

  assign S = DATA;
endmodule

module RAMG (
  input  [7:0] ADDRESS,
  input  [7:0] DATAIN,
  input  in_3,
  output [7:0] DATAOUT
);

  RAM #(.enables("line"), .\type ("nonvolatile")) ram_1 (
    .addr(ADDRESS), .we(in_3), .clk(in_3), .din(DATAIN), .dout(DATAOUT));
endmodule

module ALUP (
  input  CP,
  input  EN,
  input  Sel,
  input  [7:0] Ina,
  input  [7:0] Inb,
  output [7:0] S,
  output [7:0] Sum,
  output Carry
);

  wire add8_1_carryout, not_1_out;
  wire [7:0] inv8_1_outa;

  Inv8 inv8_1 (.Outa(inv8_1_outa), .Sel(Sel), .Ina(Inb));
  Add8 add8_1 (.out_4(S), .Carryout(add8_1_carryout), .CarryIn(Sel), .Ina(Ina), .Inb(inv8_1_outa));
  not not_1 (not_1_out, Sel);
  and and_1 (Carry, not_1_out, add8_1_carryout);
  GATA8 gata8_1 (.DATAOUT(Sum), .DATA(S), .SEL(EN));
endmodule

module ROMS (
  input  [7:0] in_1,
  output [15:0] out_2
);

  ROM #(.dataWidth(16)) rom_1 (.addr(in_1), .data(out_2));

  // Notes on the sheet:
  //   contents of rom_1 (hex, n*v repeats v):
  //   1e03 1e0c b0 1f20 8020
endmodule

module AND8 (
  input  [7:0] in_1,
  input  [7:0] in_2,
  output [7:0] out_3
);

  and and_1 (out_3[0], in_1[0], in_2[0]);
  and and_2 (out_3[1], in_1[1], in_2[1]);
  and and_3 (out_3[2], in_1[2], in_2[2]);
  and and_4 (out_3[3], in_1[3], in_2[3]);
  and and_5 (out_3[4], in_1[4], in_2[4]);
  and and_6 (out_3[5], in_1[5], in_2[5]);
  and and_7 (out_3[6], in_1[6], in_2[6]);
  and and_8 (out_3[7], in_1[7], in_2[7]);
endmodule

module OR8 (
  input  [7:0] in_1,
  input  [7:0] in_2,
  output [7:0] out_3
);

  or or_1 (out_3[0], in_1[0], in_2[0]);
  or or_2 (out_3[1], in_1[1], in_2[1]);
  or or_3 (out_3[2], in_1[2], in_2[2]);
  or or_4 (out_3[3], in_1[3], in_2[3]);
  or or_5 (out_3[4], in_1[4], in_2[4]);
  or or_6 (out_3[5], in_1[5], in_2[5]);
  or or_7 (out_3[6], in_1[6], in_2[6]);
  or or_8 (out_3[7], in_1[7], in_2[7]);
endmodule

module XOR8 (
  input  [7:0] in_1,
  input  [7:0] in_2,
  output [7:0] out_3
);

  xor xor_1 (out_3[0], in_1[0], in_2[0]);
  xor xor_2 (out_3[1], in_1[1], in_2[1]);
  xor xor_3 (out_3[2], in_1[2], in_2[2]);
  xor xor_4 (out_3[3], in_1[3], in_2[3]);
  xor xor_5 (out_3[4], in_1[4], in_2[4]);
  xor xor_6 (out_3[5], in_1[5], in_2[5]);
  xor xor_7 (out_3[6], in_1[6], in_2[6]);
  xor xor_8 (out_3[7], in_1[7], in_2[7]);
endmodule

module ALUPP (
  input  [7:0] Ina,
  input  [7:0] Inb,
  input  in_3,
  input  [2:0] Sel,
  input  in_5,
  input  in_6,
  input  EN,
  output [2:0] out_8,
  output [7:0] S,
  output [7:0] Sum
);

  wire add8_1_carryout, add8_2_carryout, and_1_out, nand_1_out, not_1_out;
  wire [3:0] or_1_out;
  wire [7:0] add8_1_out_4, add8_2_out_4, and8_1_out_3, equal38_1_outo, inv8_1_outa, inv8_2_outa, or8_1_out_3,
       xor8_1_out_3;
  wire [7:3] regbp_1_s;

  EQUAL38 equal38_1 (.OUTO(equal38_1_outo), .C(Sel[2]), .B(Sel[1]), .A(Sel[0]), .EN(1'b1));
  not not_1 (not_1_out, 1'b1);
  Add8 add8_1 (.out_4(add8_1_out_4), .Carryout(add8_1_carryout), .CarryIn(not_1_out), .Ina(Ina), .Inb(Inb));
  GATA8 gata8_1 (.DATAOUT(S), .DATA(add8_1_out_4), .SEL(equal38_1_outo[0]));
  Add8 add8_2 (.out_4(add8_2_out_4), .Carryout(add8_2_carryout), .CarryIn(1'b1), .Ina(Ina), .Inb(inv8_1_outa));
  GATA8 gata8_2 (.DATAOUT(S), .DATA(add8_2_out_4), .SEL(equal38_1_outo[1]));
  and and_1 (and_1_out, equal38_1_outo[0], add8_1_carryout);
  nand nand_1 (nand_1_out, equal38_1_outo[1], add8_2_carryout);
  Inv8 inv8_1 (.Outa(inv8_1_outa), .Sel(1'b1), .Ina(Inb));
  or or_1 (or_1_out[0], and_1_out, nand_1_out);
  GATA8 gata8_3 (.DATAOUT(Sum), .DATA(S), .SEL(EN));
  AND8 and8_1 (.out_3(and8_1_out_3), .in_2(Inb), .in_1(Ina));
  GATA8 gata8_4 (.DATAOUT(S), .DATA(and8_1_out_3), .SEL(equal38_1_outo[2]));
  nor nor_1 (or_1_out[1], S[0], S[1], S[2], S[3], S[4], S[5], S[6], S[7]);
  OR8 or8_1 (.out_3(or8_1_out_3), .in_2(Inb), .in_1(Ina));
  GATA8 gata8_5 (.DATAOUT(S), .DATA(or8_1_out_3), .SEL(equal38_1_outo[3]));
  not not_2 (or_1_out[3], 1'b1);
  XOR8 xor8_1 (.out_3(xor8_1_out_3), .in_2(Inb), .in_1(Ina));
  GATA8 gata8_6 (.DATAOUT(S), .DATA(xor8_1_out_3), .SEL(equal38_1_outo[4]));
  REGBP regbp_1 (
    .S({regbp_1_s, out_8}), .PRE(in_5), .CLOCK(in_6), .DATA({{5{or_1_out[3]}}, S[0], or_1_out[1:0]}),
    .CLEAR(in_3), .WE(1'b1), .CS(1'b1));  // open: DATAout
  Inv8 inv8_2 (.Outa(inv8_2_outa), .Sel(1'b1), .Ina(Ina));
  GATA8 gata8_7 (.DATAOUT(S), .DATA(inv8_2_outa), .SEL(equal38_1_outo[5]));
endmodule

module DELREG (
  input  [4:0] w,
  input  [4:0] r,
  output [1:0] A,
  output [1:0] CS,
  output [1:0] B,
  output [1:0] MSR,
  output [1:0] DS,
  output [1:0] C,
  output [1:0] MAR,
  output [1:0] SS,
  output [1:0] D,
  output [1:0] MDR,
  output [1:0] ES,
  output [1:0] DI,
  output [1:0] MC,
  output [1:0] VEC,
  output [1:0] SI,
  output [1:0] IR,
  output [1:0] T1,
  output [1:0] SP,
  output [1:0] DST,
  output [1:0] T2,
  output [1:0] BP,
  output [1:0] SRC
);

  wire [0:0] equal532_1_d;
  wire [7:0] equal532_1_d_3;
  wire [23:23] equal532_1_d_2;
  wire [31:0] equal532_2_d, xor32_1_out_3;

  equal532 equal532_1 (
    .D({equal532_1_d_3, equal532_1_d_2[23], T2[0], T1[0], VEC[0], ES[0], SS[0], DS[0], CS[0], BP[0], SP[0], SI[0], DI[0], D[0], C[0], B[0], A[0], SRC[0], DST[0], IR[0], MC[0], MDR[0], MAR[0], MSR[0], equal532_1_d[0]}),
    .A(w));
  equal532 equal532_2 (.D(equal532_2_d), .A(r));
  XOR32 xor32_1 (
    .out_3({xor32_1_out_3[31:23], T2[1], T1[1], VEC[1], ES[1], SS[1], DS[1], CS[1], BP[1], SP[1], SI[1], DI[1], D[1], C[1], B[1], A[1], SRC[1], DST[1], IR[1], MC[1], MDR[1], MAR[1], MSR[1], xor32_1_out_3[0]}),
    .in_2(equal532_2_d),
    .in_1({equal532_1_d_3, equal532_1_d_2[23], T2[0], T1[0], VEC[0], ES[0], SS[0], DS[0], CS[0], BP[0], SP[0], SI[0], DI[0], D[0], C[0], B[0], A[0], SRC[0], DST[0], IR[0], MC[0], MDR[0], MAR[0], MSR[0], equal532_1_d[0]}));
endmodule

module equal532 (
  input  [4:0] A,
  output [31:0] D
);

  ROM #(.addrWidth(5), .dataWidth(32)) rom_1 (.addr(A), .data(D));

  // Notes on the sheet:
  //   contents of rom_1 (hex, n*v repeats v):
  //   1 2 4 8 10 20 40 80 100 200 400 800 1000 2000 4000 8000 10000 20000 40000 80000 100000 200000 400000
  //   800000 1000000 2000000 4000000 8000000 10000000 20000000 40000000 80000000
endmodule

module REGBPP (
  input  [7:0] DATA,
  input  CLOCK,
  input  PRE,
  input  CLEAR,
  input  [1:0] IO,
  output [7:0] S,
  output [7:0] DATAout
);

  wire and_1_out, and_2_out, not_1_out;

  and and_1 (and_1_out, IO[0], IO[1], CLOCK);
  REGB regb_1 (.DATAOUT(S), .DATA(DATA), .Pre(PRE), .CLOCK(and_1_out), .Clear(CLEAR));
  and and_2 (and_2_out, not_1_out, IO[1]);
  GATA8 gata8_1 (.DATAOUT(DATAout), .DATA(S), .SEL(and_2_out));
  not not_1 (not_1_out, IO[0]);
endmodule

module PCP (
  input  [2:0] EN,
  input  [7:0] DATA,
  input  CLEAR,
  input  PRE,
  input  CLOCK,
  output [7:0] S,
  output [7:0] OUTDATA
);

  wire not_1_out;
  wire [7:0] add8_1_out_4, gata8_1_dataout;

  not not_1 (not_1_out, EN[2]);
  GATA8 gata8_1 (.DATAOUT(gata8_1_dataout), .DATA(DATA), .SEL(not_1_out));
  REGBPP regbpp_1 (
    .DATAout(OUTDATA), .S(S), .PRE(PRE), .CLOCK(CLOCK), .DATA(gata8_1_dataout), .CLEAR(CLEAR), .IO(EN[1:0]));
  Add8 add8_1 (.out_4(add8_1_out_4), .CarryIn(1'b0), .Ina(S), .Inb(8'h1));  // open: Carryout
  GATA8 gata8_2 (.DATAOUT(gata8_1_dataout), .DATA(add8_1_out_4), .SEL(EN[2]));
endmodule

module ALUPPP (
  input  [7:0] Ina,
  input  [7:0] Inb,
  input  [2:0] Sel,
  input  [3:0] EN,
  input  CLEAR,
  input  CLOCK,
  input  PRE,
  output [3:0] out_8,
  output [7:0] S,
  output [7:0] Sum
);

  wire add8_1_carryout, add8_2_carryout, and_1_out, and_2_out, not_1_out;
  wire [1:1] or_1_out;
  wire [3:1] nor_1_out;
  wire [7:0] add8_1_out_4, add8_2_out_4, and8_1_out_3, equal38_1_outo, inv8_1_outa, inv8_2_outa, or8_1_out_3,
       xor8_1_out_3;
  wire [7:4] regbpp_1_s;

  EQUAL38 equal38_1 (.OUTO(equal38_1_outo), .C(Sel[2]), .B(Sel[1]), .A(Sel[0]), .EN(1'b1));
  not not_1 (not_1_out, 1'b1);
  Add8 add8_1 (.out_4(add8_1_out_4), .Carryout(add8_1_carryout), .CarryIn(not_1_out), .Ina(Ina), .Inb(Inb));
  GATA8 gata8_1 (.DATAOUT(S), .DATA(add8_1_out_4), .SEL(equal38_1_outo[0]));
  Add8 add8_2 (.out_4(add8_2_out_4), .Carryout(add8_2_carryout), .CarryIn(1'b1), .Ina(Ina), .Inb(inv8_1_outa));
  GATA8 gata8_2 (.DATAOUT(S), .DATA(add8_2_out_4), .SEL(equal38_1_outo[1]));
  and and_1 (and_1_out, equal38_1_outo[0], add8_1_carryout);
  and and_2 (and_2_out, equal38_1_outo[1], add8_2_carryout);
  Inv8 inv8_1 (.Outa(inv8_1_outa), .Sel(1'b1), .Ina(Inb));
  or or_1 (or_1_out[1], and_1_out, and_2_out);
  GATA8 gata8_3 (.DATAOUT(Sum), .DATA(S), .SEL(EN[0]));
  AND8 and8_1 (.out_3(and8_1_out_3), .in_2(Inb), .in_1(Ina));
  GATA8 gata8_4 (.DATAOUT(S), .DATA(and8_1_out_3), .SEL(equal38_1_outo[2]));
  nor nor_1 (nor_1_out[1], S[0], S[1], S[2], S[3], S[4], S[5], S[6], S[7]);
  OR8 or8_1 (.out_3(or8_1_out_3), .in_2(Inb), .in_1(Ina));
  GATA8 gata8_5 (.DATAOUT(S), .DATA(or8_1_out_3), .SEL(equal38_1_outo[3]));
  not not_2 (nor_1_out[3], or_1_out[1]);
  XOR8 xor8_1 (.out_3(xor8_1_out_3), .in_2(Inb), .in_1(Ina));
  GATA8 gata8_6 (.DATAOUT(S), .DATA(xor8_1_out_3), .SEL(equal38_1_outo[4]));
  REGBPP regbpp_1 (
    .S({regbpp_1_s, out_8}), .PRE(PRE), .CLOCK(CLOCK),
    .DATA({{5{nor_1_out[3]}}, S[0], nor_1_out[1], or_1_out[1]}), .CLEAR(CLEAR), .IO({2{or_1_out[1]}}));  // open: DATAout
  Inv8 inv8_2 (.Outa(inv8_2_outa), .Sel(1'b1), .Ina(Ina));
  GATA8 gata8_7 (.DATAOUT(S), .DATA(inv8_2_outa), .SEL(equal38_1_outo[5]));
endmodule

module RAMP (
  input  [15:0] ADDRESS,
  input  [7:0] DATAIN,
  input  in_3,
  output [7:0] DATAOUT
);

  RAM #(.addrWidth(16), .enables("line"), .\type ("nonvolatile")) ram_1 (
    .addr(ADDRESS), .we(in_3), .clk(in_3), .din(DATAIN), .dout(DATAOUT));
endmodule

module MC (
  input  CLOCK,
  input  [7:0] DATA,
  input  [1:0] IO,
  output W,
  output [7:0] S,
  output [7:0] DATAout
);

  wire and_2_out, not_1_out;

  and and_1 (W, IO[0], IO[1], CLOCK);
  and and_2 (and_2_out, not_1_out, IO[1]);
  GATA8 gata8_1 (.DATAOUT(DATAout), .DATA(DATA), .SEL(and_2_out));
  not not_1 (not_1_out, IO[0]);

  assign S = DATA;
endmodule

module RCF (
  input  [4:0] DC,
  input  [4:0] RC,
  input  [7:0] D,
  input  DW,
  input  DR,
  input  [7:0] S,
  input  SR,
  input  SW,
  output [4:0] W,
  output [4:0] R
);

  wire [7:0] equal821_1_out_4, equal821_3_out_4;
  wire [7:5] equal821_2_out_4, equal821_4_out_4;

  EQUAL821 equal821_1 (.out_4(equal821_1_out_4), .Ina(D), .Inb({3'b000, DC}), .EN(DW));
  EQUAL821 equal821_2 (.out_4({equal821_2_out_4, W}), .Ina(S), .Inb(equal821_1_out_4), .EN(SW));
  EQUAL821 equal821_3 (.out_4(equal821_3_out_4), .Ina(D), .Inb({3'b000, RC}), .EN(DR));
  EQUAL821 equal821_4 (.out_4({equal821_4_out_4, R}), .Ina(S), .Inb(equal821_3_out_4), .EN(SR));
endmodule

module EQUAL821 (
  input  EN,
  input  [7:0] Ina,
  input  [7:0] Inb,
  output [7:0] out_4
);

  SEL21 sel21_1 (.OUTOUT(out_4[0]), .EN(EN), .A(Ina[0]), .B(Inb[0]));
  SEL21 sel21_2 (.OUTOUT(out_4[1]), .EN(EN), .A(Ina[1]), .B(Inb[1]));
  SEL21 sel21_3 (.OUTOUT(out_4[2]), .EN(EN), .A(Ina[2]), .B(Inb[2]));
  SEL21 sel21_4 (.OUTOUT(out_4[3]), .EN(EN), .A(Ina[3]), .B(Inb[3]));
  SEL21 sel21_5 (.OUTOUT(out_4[4]), .EN(EN), .A(Ina[4]), .B(Inb[4]));
  SEL21 sel21_6 (.OUTOUT(out_4[5]), .EN(EN), .A(Ina[5]), .B(Inb[5]));
  SEL21 sel21_7 (.OUTOUT(out_4[6]), .EN(EN), .A(Ina[6]), .B(Inb[6]));
  SEL21 sel21_8 (.OUTOUT(out_4[7]), .EN(EN), .A(Ina[7]), .B(Inb[7]));
endmodule

module SEL21 (
  input  A,
  input  B,
  input  EN,
  output OUTOUT
);

  wire and_1_out, and_2_out, not_1_out;

  not not_1 (not_1_out, EN);
  and and_1 (and_1_out, EN, A);
  and and_2 (and_2_out, not_1_out, B);
  or or_1 (OUTOUT, and_1_out, and_2_out);
endmodule

module CONTROL (
  input  [31:0] DD,
  input  CLOCK,
  input  CLEAR,
  input  [7:0] R2,
  input  [7:0] R3,
  input  [3:0] ALU,
  input  [3:0] PSW,
  input  [7:0] R1,
  output HLT,
  output [1:0] MSR,
  output [1:0] MAR,
  output [1:0] MDR,
  output [1:0] MC,
  output [3:0] CYC,
  output [2:0] OP,
  output [1:0] A,
  output [1:0] B,
  output [1:0] C,
  output [2:0] PC,
  output [1:0] IR,
  output [1:0] D,
  output [1:0] DST,
  output [1:0] VEC,
  output [1:0] SRC,
  output [1:0] T1,
  output [1:0] T2,
  output [1:0] CS,
  output [1:0] BP,
  output [15:0] AA,
  output [1:0] DS,
  output [1:0] SP,
  output [1:0] SS,
  output [1:0] SI,
  output [1:0] ES,
  output [1:0] DI
);

  wire not_1_out;
  wire [2:1] or_1_out;
  wire [4:0] rcf_1_r, rcf_1_w;
  wire [7:4] pcp_1_s;

  not not_1 (not_1_out, CLOCK);
  PCP pcp_1 (
    .S({pcp_1_s, AA[3:0]}), .EN({or_1_out, or_1_out[1]}), .DATA({8{1'b0}}), .CLEAR(CLEAR), .PRE(1'b0),
    .CLOCK(not_1_out));  // open: OUTDATA
  or or_1 (or_1_out[1], 1'b1, DD[30]);
  not not_2 (or_1_out[2], DD[30]);
  RCF rcf_1 (
    .W(rcf_1_w), .R(rcf_1_r), .DC(DD[9:5]), .DW(DD[13]), .SW(DD[11]), .RC(DD[4:0]), .DR(DD[12]), .SR(DD[10]),
    .D(R2), .S(R3));
  DELREG delreg_1 (
    .CS(CS), .DS(DS), .SS(SS), .ES(ES), .VEC(VEC), .T1(T1), .T2(T2), .A(A), .B(B), .C(C), .D(D), .DI(DI),
    .SI(SI), .SP(SP), .BP(BP), .MSR(MSR), .MAR(MAR), .MDR(MDR), .MC(MC), .IR(IR), .DST(DST), .SRC(SRC),
    .w(rcf_1_w), .r(rcf_1_r));

  assign AA[15:4] = {R1, PSW};
  assign CYC = AA[3:0];
  assign DD[23:20] = ALU;
  assign HLT = DD[31];
  assign OP = DD[19:17];
  assign PC = DD[16:14];
endmodule

module XOR32 (
  input  [31:0] in_1,
  input  [31:0] in_2,
  output [31:0] out_3
);

  XOR8 xor8_1 (.out_3(out_3[7:0]), .in_2(in_2[7:0]), .in_1(in_1[7:0]));
  XOR8 xor8_2 (.out_3(out_3[15:8]), .in_2(in_2[15:8]), .in_1(in_1[15:8]));
  XOR8 xor8_3 (.out_3(out_3[23:16]), .in_2(in_2[23:16]), .in_1(in_1[23:16]));
  XOR8 xor8_4 (.out_3(out_3[31:24]), .in_2(in_2[31:24]), .in_1(in_1[31:24]));
endmodule
